// Logisim project e2580751.circ as structural Verilog: 1 circuit, main circuit main
module main (
  input  A1,
  input  A0,
  input  B1,
  input  B0,
  input  O0,
  input  O1,
  input  O2,
  input  O3,
  output P,
  output Z,
  output L0,
  output L1,
  output L2,
  output L3,
  output L4,
  output L5,
  output L6,
  output L7,
  output L8,
  output E,
  output L9,
  output G,
  output C,
  output L,
  output S
);

  wire and_1_out, and_2_out, and_3_out, and_4_out, and_5_out, and_6_out, and_7_out, and_8_out, and_9_out,
       and_10_out, and_11_out, and_12_out, and_13_out, and_14_out, and_15_out, and_16_out, and_17_out,
       and_18_out, and_19_out, and_20_out, and_24_out, and_25_out, and_26_out, and_27_out, and_28_out,
       and_29_out, and_33_out, and_34_out, and_35_out, and_36_out, and_37_out, and_38_out, and_39_out,
       and_40_out, and_41_out, and_42_out, and_43_out, and_44_out, and_45_out, and_46_out, and_47_out,
       and_48_out, and_49_out, and_50_out, and_51_out, and_52_out, and_53_out, and_54_out, and_55_out,
       and_56_out, and_57_out, and_58_out, and_59_out, and_60_out, and_61_out, and_62_out, and_63_out,
       and_64_out, and_65_out, controlled_buffer_1_out, controlled_buffer_2_out, controlled_buffer_3_out,
       controlled_buffer_4_out, n4_to_1_mux_x2_74153_1_p3, n4_to_1_mux_x2_74153_1_p4,
       n4_to_1_mux_x2_74153_1_p5, n4_to_1_mux_x2_74153_1_p8, n4_to_1_mux_x2_74153_1_p12,
       n4_to_1_mux_x2_74153_1_p13, n4_to_1_mux_x2_74153_2_p5, n4_to_1_mux_x2_74153_2_p8,
       n4_to_1_mux_x2_74153_2_p12, n4_to_1_mux_x2_74153_2_p13, n4_to_1_mux_x2_74153_3_p12,
       n4_to_1_mux_x2_74153_3_p13, not_1_out, not_2_out, not_3_out, not_4_out, not_7_out, not_9_out,
       not_10_out, not_11_out, not_15_out, not_17_out, not_19_out, not_20_out, not_21_out, not_22_out,
       or_1_out, or_2_out, or_3_out, or_4_out, or_5_out, or_6_out, or_7_out, or_8_out, or_10_out, or_11_out,
       or_12_out, or_13_out, or_14_out, or_15_out, or_16_out, or_17_out, or_18_out, or_19_out, or_21_out,
       or_22_out, or_23_out, or_24_out, or_25_out, or_26_out, xor_2_out, xor_3_out;

  not not_1 (not_1_out, A1);
  not not_2 (not_2_out, A0);
  not not_3 (not_3_out, B1);
  not not_4 (not_4_out, B0);
  and and_1 (and_1_out, A0, B1);
  and and_2 (and_2_out, and_1_out, not_1_out);
  and and_3 (and_3_out, and_1_out, not_4_out);
  and and_4 (and_4_out, not_2_out, A1);
  and and_5 (and_5_out, and_4_out, and_6_out);
  or or_1 (or_1_out, and_3_out, and_2_out);
  and and_6 (and_6_out, B1, B0);
  and and_7 (and_7_out, and_9_out, and_8_out);
  and and_8 (and_8_out, B1, B0);
  and and_9 (and_9_out, A1, A0);
  // _3_to_8_decoder__74138 #(.Facing("east")) 3_to_8_decoder_74138_1: pin names not known; wires that end beside it: O0, O1, O2, O3, O3
  or or_2 (or_2_out, and_10_out, and_12_out);
  and and_10 (and_10_out, not_2_out, and_11_out);
  and and_11 (and_11_out, A1, B1);
  // NOT_Gate not_5 has open pins: in=O3, out=open
  and and_12 (and_12_out, and_11_out, not_4_out);
  and and_13 (and_13_out, A1, B1);
  // NOT_Gate not_6 is placed but not wired
  // NOT_Gate not_7 has open pins: in=open, out=not_7_out
  // NOT_Gate not_8 is placed but not wired
  // NOT_Gate not_9 has open pins: in=open, out=not_9_out
  // NOT_Gate not_10 has open pins: in=open, out=not_10_out
  // NOT_Gate not_11 has open pins: in=open, out=not_11_out
  // NOT_Gate not_12 is placed but not wired
  // NOT_Gate not_13 is placed but not wired
  and and_14 (and_14_out, not_1_out, and_17_out);
  and and_15 (and_15_out, A0, B0);
  or or_3 (or_3_out, or_4_out, or_5_out);
  or or_4 (or_4_out, and_14_out, and_16_out);
  and and_16 (and_16_out, and_17_out, not_4_out);
  and and_17 (and_17_out, A0, B1);
  or or_5 (or_5_out, and_19_out, and_18_out);
  and and_18 (and_18_out, and_20_out, not_3_out);
  and and_19 (and_19_out, not_2_out, and_20_out);
  and and_20 (and_20_out, A1, B0);
  and and_21 (L9, not_7_out, and_7_out);
  and and_22 (C, not_9_out, or_15_out);
  and and_23 (S, not_10_out, or_12_out);
  and and_24 (and_24_out, A0, B0);
  and and_25 (and_25_out, A1, not_3_out);
  and and_26 (and_26_out, A0, not_4_out);
  and and_27 (and_27_out, and_26_out, not_3_out);
  or or_6 (or_6_out, and_25_out, or_7_out);
  or or_7 (or_7_out, and_27_out, and_29_out);
  and and_28 (and_28_out, A1, and_34_out);
  and and_29 (and_29_out, and_26_out, A1);
  and and_30 (E, or_23_out, not_11_out);
  and and_31 (G, or_6_out, not_11_out);
  and and_32 (L, or_12_out, not_11_out);
  or or_8 (or_8_out, and_28_out, and_33_out);
  and and_33 (and_33_out, and_34_out, not_3_out);
  and and_34 (and_34_out, A0, B0);
  // _4_to_1_MUX__x2___74153 #(.Facing("east")) 4_to_1_mux_x2_74153_1: pin names not known; wires that end beside it: or_1_out, and_24_out, n4_to_1_mux_x2_74153_1_p3, n4_to_1_mux_x2_74153_1_p4, n4_to_1_mux_x2_74153_1_p5, 1'b0, and_15_out, n4_to_1_mux_x2_74153_1_p8, O2, O0, O1, n4_to_1_mux_x2_74153_1_p12, n4_to_1_mux_x2_74153_1_p13
  // NOT_Gate not_14 has open pins: in=O2, out=open
  or or_9 (n4_to_1_mux_x2_74153_1_p3, or_8_out, and_35_out);
  and and_35 (and_35_out, B1, and_36_out);
  and and_36 (and_36_out, A1, not_4_out);
  and and_37 (and_37_out, A1, and_38_out);
  and and_38 (and_38_out, B0, not_3_out);
  assign controlled_buffer_1_out = O3 ? or_16_out : 1'bz;  // Controlled_Buffer controlled_buffer_1
  assign controlled_buffer_2_out = not_15_out ? or_10_out : 1'bz;  // Controlled_Buffer controlled_buffer_2
  or or_10 (or_10_out, n4_to_1_mux_x2_74153_1_p12, n4_to_1_mux_x2_74153_1_p13);
  not not_15 (not_15_out, O3);
  and and_39 (and_39_out, not_1_out, B1);
  or or_11 (or_11_out, controlled_buffer_1_out, controlled_buffer_2_out);
  and and_40 (and_40_out, not_2_out, B0);
  and and_41 (and_41_out, and_40_out, B1);
  or or_12 (or_12_out, and_39_out, or_13_out);
  xor xor_1 (n4_to_1_mux_x2_74153_1_p4, A0, B0);
  and and_42 (and_42_out, A0, B0);
  and and_43 (and_43_out, and_40_out, not_1_out);
  or or_13 (or_13_out, and_41_out, and_43_out);
  and and_44 (and_44_out, and_42_out, xor_3_out);
  xor xor_2 (xor_2_out, and_42_out, xor_3_out);
  xor xor_3 (xor_3_out, A1, B1);
  or or_14 (or_14_out, A1, B1);
  or or_15 (or_15_out, and_44_out, and_45_out);
  and and_45 (and_45_out, A1, B1);
  or or_16 (or_16_out, A0, B0);
  // _4_to_1_MUX__x2___74153 #(.Facing("east")) 4_to_1_mux_x2_74153_2: pin names not known; wires that end beside it: and_5_out, or_3_out, and_37_out, xor_2_out, n4_to_1_mux_x2_74153_2_p5, 1'b0, and_13_out, n4_to_1_mux_x2_74153_2_p8, O2, O0, O1, n4_to_1_mux_x2_74153_2_p12, n4_to_1_mux_x2_74153_2_p13
  xor xor_4 (n4_to_1_mux_x2_74153_2_p8, A1, B1);
  // NOT_Gate not_16 has open pins: in=O2, out=open
  and and_46 (and_46_out, and_47_out, not_3_out);
  and and_47 (and_47_out, A1, A0);
  xor xor_5 (n4_to_1_mux_x2_74153_1_p8, A0, B0);
  assign controlled_buffer_3_out = O3 ? or_14_out : 1'bz;  // Controlled_Buffer controlled_buffer_3
  or or_17 (or_17_out, n4_to_1_mux_x2_74153_2_p12, n4_to_1_mux_x2_74153_2_p13);
  not not_17 (not_17_out, O3);
  or or_18 (or_18_out, and_46_out, and_48_out);
  and and_48 (and_48_out, and_49_out, B1);
  and and_49 (and_49_out, not_1_out, not_2_out);
  or or_19 (or_19_out, controlled_buffer_3_out, controlled_buffer_4_out);
  assign controlled_buffer_4_out = not_17_out ? or_17_out : 1'bz;  // Controlled_Buffer controlled_buffer_4
  or or_20 (n4_to_1_mux_x2_74153_2_p5, or_18_out, or_21_out);
  or or_21 (or_21_out, and_50_out, and_52_out);
  and and_50 (and_50_out, and_51_out, A1);
  and and_51 (and_51_out, not_3_out, not_4_out);
  and and_52 (and_52_out, and_53_out, not_1_out);
  and and_53 (and_53_out, B0, B1);
  xor xor_6 (n4_to_1_mux_x2_74153_1_p5, A0, B0);
  and and_54 (and_54_out, not_1_out, not_2_out);
  and and_55 (and_55_out, and_54_out, and_56_out);
  and and_56 (and_56_out, not_3_out, not_4_out);
  or or_22 (or_22_out, and_55_out, and_59_out);
  and and_57 (and_57_out, A1, not_2_out);
  and and_58 (and_58_out, B1, not_4_out);
  and and_59 (and_59_out, and_57_out, and_58_out);
  and and_60 (and_60_out, not_1_out, A0);
  and and_61 (and_61_out, and_60_out, and_62_out);
  or or_23 (or_23_out, or_22_out, or_24_out);
  and and_62 (and_62_out, not_3_out, B0);
  and and_63 (and_63_out, A1, A0);
  or or_24 (or_24_out, and_61_out, and_65_out);
  and and_64 (and_64_out, B1, B0);
  and and_65 (and_65_out, and_63_out, and_64_out);
  // _4_to_1_MUX__x2___74153 #(.Facing("east")) 4_to_1_mux_x2_74153_3: pin names not known; wires that end beside it: 1'b0, or_2_out, 1'b0, or_15_out, 1'b0, 1'b0, 1'b0, 1'b0, O2, O0, O1, n4_to_1_mux_x2_74153_3_p12, n4_to_1_mux_x2_74153_3_p13
  // NOT_Gate not_18 has open pins: in=O2, out=open
  or or_25 (or_25_out, n4_to_1_mux_x2_74153_3_p12, n4_to_1_mux_x2_74153_3_p13);
  or or_26 (or_26_out, L4, L1);
  not not_19 (not_19_out, not_11_out);
  not not_20 (not_20_out, L9);
  and and_66 (L1, not_20_out, not_22_out);
  or or_27 (P, or_26_out, L2);
  and and_67 (L0, not_19_out, not_21_out);
  // _3_to_8_decoder__74138 #(.Facing("east")) 3_to_8_decoder_74138_2: pin names not known; wires that end beside it: or_11_out, or_19_out, or_25_out, 1'b1, 1'b0
  // NOT_Gate not_21 has open pins: in=open, out=not_21_out
  // NOT_Gate not_22 has open pins: in=open, out=not_22_out
  // NOT_Gate not_23 has open pins: in=open, out=L2
  // NOT_Gate not_24 has open pins: in=open, out=L3
  // NOT_Gate not_25 has open pins: in=open, out=L4
  // NOT_Gate not_26 has open pins: in=open, out=L5
  // NOT_Gate not_27 has open pins: in=open, out=L6
  // NOT_Gate not_28 has open pins: in=open, out=L7

  assign L8 = 1'b0;
  assign Z = L0;
endmodule
