// Logisim project helper.circ as structural Verilog: 1 circuit, main circuit main
module main (
  input  _2,
  input  in_2,
  input  \or ,
  input  _3,
  input  in_5,
  input  in_6,
  input  in_7,
  input  in_8,
  input  _3_2,
  input  compare,
  input  \and ,
  input  \xor ,
  input  in_13,
  input  _0,
  input  _1,
  input  _0_2,
  input  _1_2,
  input  _2_2,
  input  _3_3,
  output out_20
);

  wire controlled_buffer_1_out, controlled_buffer_2_out, n3_to_8_decoder_74138_1_p6,
       n3_to_8_decoder_74138_1_p8, n3_to_8_decoder_74138_1_p9, n3_to_8_decoder_74138_1_p10,
       n3_to_8_decoder_74138_1_p11, n3_to_8_decoder_74138_1_p12, n3_to_8_decoder_74138_1_p13,
       n3_to_8_decoder_74138_1_p14, n3_to_8_decoder_74138_2_p7, n3_to_8_decoder_74138_2_p8,
       n4_to_1_mux_x2_74153_1_p13, n4_to_1_mux_x2_74153_1_p14, not_3_out, not_4_out, or_1_out;

  // _4_to_1_MUX__x2___74153 #(.Facing("east")) 4_to_1_mux_x2_74153_1: pin names not known; wires that end beside it: 1'b0, in_2, in_5, in_6, in_7, in_8, compare, \and , \xor , _2, _0, _1, n4_to_1_mux_x2_74153_1_p13, n4_to_1_mux_x2_74153_1_p14
  // NOT_Gate not_1 has open pins: in=_2, out=open
  // _3_to_8_decoder__74138 #(.Facing("east")) 3_to_8_decoder_74138_1: pin names not known; wires that end beside it: _0_2, _1_2, _2_2, _3_3, _3_3, n3_to_8_decoder_74138_1_p6, n3_to_8_decoder_74138_1_p6, n3_to_8_decoder_74138_1_p8, n3_to_8_decoder_74138_1_p9, n3_to_8_decoder_74138_1_p10, n3_to_8_decoder_74138_1_p11, n3_to_8_decoder_74138_1_p12, n3_to_8_decoder_74138_1_p13, n3_to_8_decoder_74138_1_p14, n3_to_8_decoder_74138_1_p8, n3_to_8_decoder_74138_1_p9, n3_to_8_decoder_74138_1_p10, n3_to_8_decoder_74138_1_p11, n3_to_8_decoder_74138_1_p12, n3_to_8_decoder_74138_1_p13
  // NOT_Gate not_2 has open pins: in=_3_3, out=open
  not not_3 (not_3_out, _3_3);
  assign controlled_buffer_1_out = _3 ? \or  : 1'bz;  // Controlled_Buffer controlled_buffer_1
  or or_1 (or_1_out, n4_to_1_mux_x2_74153_1_p13, n4_to_1_mux_x2_74153_1_p14);
  assign controlled_buffer_2_out = not_4_out ? or_1_out : 1'bz;  // Controlled_Buffer controlled_buffer_2
  not not_4 (not_4_out, _3_2);
  // _3_to_8_decoder__74138 #(.Facing("east")) 3_to_8_decoder_74138_2: pin names not known; wires that end beside it: n3_to_8_decoder_74138_1_p14, _0_2, _1_2, _2_2, not_3_out, not_3_out, n3_to_8_decoder_74138_2_p7, n3_to_8_decoder_74138_2_p8, n3_to_8_decoder_74138_2_p7, n3_to_8_decoder_74138_2_p8
  // NOT_Gate not_5 has open pins: in=not_3_out, out=open
  // OR_Gate or_2 has open pins: in0=controlled_buffer_1_out, in1=controlled_buffer_2_out, out=open
  buf and_1 (out_20, in_13);  // AND_Gate
endmodule
